// Digital circuit +1.dig as structural Verilog
module _1 (
  input  [2:0] I_2_0,
  output [2:0] O_2_0
);

  Add #(.Bits(3)) plus_1 (.a(I_2_0), .b(3'b001), .c_i(1'b0), .s(O_2_0));  // open: c_o
endmodule
