// Digital circuit 3BitALU.dig as structural Verilog
module _3BitALU (
  input  [2:0] A_2_0,
  input  [2:0] B_2_0,
  input  [1:0] OP_1_0,
  output [2:0] R_2_0,
  output SF,
  output ZF,
  output CF
);

  wire [2:0] ADD, NOT, ROL;

  _3BitNotGate _3bitnotgate_1 (.A_2_0(A_2_0), .O_2_0(NOT));
  _3BitAdder _3bitadder_1 (.A_2_0(A_2_0), .B_2_0(B_2_0), .O_2_0(ADD), .Carry(CF));
  _3BitROL _3bitrol_1 (.A_2_0(A_2_0), .Shift_1_0(B_2_0[1:0]), .O_2_0(ROL));
  Multiplexer #(.Selector_Bits(2), .Bits(3)) multiplexer_1 (
    .sel(OP_1_0), .in_0(NOT), .in_1(ADD), .in_2(ROL), .in_3(3'b000), .out(R_2_0));
  nor nor_1 (ZF, R_2_0[0], R_2_0[1], R_2_0[2]);

  assign SF = R_2_0[2];

  // Other names for the same wires on the sheet: A[2:0] = A_2_0; B[2:0] = B_2_0; Shift[1:0] = B_2_0[1:0]; CARRY = CF
endmodule
