// Digital circuit 3BitAdder.dig as structural Verilog
module _3BitAdder (
  input  [2:0] A_2_0,
  input  [2:0] B_2_0,
  output [2:0] O_2_0,
  output Carry
);

  wire fa_2_cout, fa_3_cout;

  FA fa_1 (.Y(B_2_0[2]), .X(A_2_0[2]), .Cin(fa_2_cout), .Cout(Carry), .S(O_2_0[2]));
  FA fa_2 (.Y(B_2_0[1]), .X(A_2_0[1]), .Cin(fa_3_cout), .Cout(fa_2_cout), .S(O_2_0[1]));
  FA fa_3 (.Y(B_2_0[0]), .X(A_2_0[0]), .Cin(1'b0), .Cout(fa_3_cout), .S(O_2_0[0]));

  // Other names for the same wires on the sheet: A0 = A_2_0[0]; A1 = A_2_0[1]; A2 = A_2_0[2]; B0 = B_2_0[0];
  //   B1 = B_2_0[1]; B2 = B_2_0[2]; O0 = O_2_0[0]; O1 = O_2_0[1]; O2 = O_2_0[2]
endmodule
