// Digital circuit 3BitCPU.dig as structural Verilog
module _3BitCPU (
  input  [2:0] WA_2_0,
  input  [16:0] WD_16_0,
  input  WE,
  input  Clock,
  input  PC_EN,
  input  ZF,
  input  SF,
  input  [2:0] RA2,
  output [16:0] RD2_16_0,
  output [2:0] R_2_0,
  output [2:0] B,
  output [2:0] A,
  output [2:0] Label
);

  wire CPU_CLK, Imm_sel, Jmp_sel, REG_EN;
  wire [1:0] Op;
  wire [2:0] _1_1_o_2_0, _3bitregset_1_b_2_0, multiplexer_1_out, reg1, reg2_imm;
  wire [3:0] Opcode;
  wire [6:0] _7x17sram_1_rd1_16_0;

  Multiplexer #(.Bits(3)) multiplexer_1 (.sel(Jmp_sel), .in_0(_1_1_o_2_0), .in_1(reg1), .out(multiplexer_1_out));
  _1 _1_1 (.I_2_0(Label), .O_2_0(_1_1_o_2_0));
  _3bitProgramCounter _3bitprogramcounter_1 (.I_2_0(multiplexer_1_out), .CPU_CLK(CPU_CLK), .O_2_0(Label));
  and and_1 (CPU_CLK, PC_EN, Clock);
  _7x17SRAM _7x17sram_1 (
    .RA1_2_0(Label), .RA2_2_0(RA2), .WA_2_0(WA_2_0), .WD_16_0(WD_16_0), .WE(WE), .Clock(Clock),
    .RD1_16_0({Opcode, reg1, reg2_imm, _7x17sram_1_rd1_16_0}), .RD2_16_0(RD2_16_0));
  _3BitRegSet _3bitregset_1 (
    .Wr_2_0(reg1), .Clock(CPU_CLK), .REG_EN(REG_EN), .Wrd_2_0(R_2_0), .A_2_0(A), .B_2_0(_3bitregset_1_b_2_0),
    .Ra_2_0(reg1), .Rb_2_0(reg2_imm));
  _3BitALU _3bitalu_1 (.A_2_0(A), .B_2_0(B), .OP_1_0(Op), .R_2_0(R_2_0));  // open: CF, SF, ZF
  Control_Unit control_unit_1 (
    .Opcode_3_0(Opcode), .Op_1_0(Op), .REG_EN(REG_EN), .Imm_sel(Imm_sel), .Jmp_sel(Jmp_sel), .ZF(ZF), .SF(SF));
  Multiplexer #(.Bits(3)) multiplexer_2 (.sel(Imm_sel), .in_0(_3bitregset_1_b_2_0), .in_1(reg2_imm), .out(B));

  // Other names for the same wires on the sheet: Clk = Clock; WA[2:0] = WA_2_0; WD[16:0] = WD_16_0

  // Notes on the sheet:
  //   COMMANDS:
  //   000----ADD R0,3
  //   001----ADD R1,2
  //   010----ADD R0,R1
  //   011----JE 010
  //   100----ROL R1,2
  //   101----NOT R1
  //   110----JMP 100
  //   MACHINE CODE:
  //   000----01010000110000000
  //   001----01010010100000000
  //   010----00010000010000000
  //   011----10010100000000000
  //   100----01100010100000000
  //   101----00000010000000000
  //   110----10001000000000000
  //   Register mode(00) = 2bit (Type of mode)+2bit(op) + 3bit(reg 1) + 3bit(reg 2) + 7bit(dont care)
  //   Immediate mode(01) = 2bit (Type of mode)+2bit(op) + 3bit(reg 1) + 3bit(imm value) + 7bit(dont care
  //   NOT op = 00
  //   ADD op = 01
  //   ROL op = 10
  //   Branching (10) = 2bit(Type of mode) + 2bit(op) + 3bit(jmp label for JE)
  //   JMP op = 00    ,    JE    op = 01
  //   R0----011
  //   R1----010
  //   R0----101 (R0+R1)
  //   R0----111 (R0+R1)
  //   R1----001 (ROL R1,2)
  //   R1----110 (NOT R1)
  //   R1----100 (ROL R1,2)
endmodule
