// Digital circuit 3BitNotGate.dig as structural Verilog
module _3BitNotGate (
  input  [2:0] A_2_0,
  output [2:0] O_2_0
);

  not not_1 (O_2_0[0], A_2_0[0]);
  not not_2 (O_2_0[1], A_2_0[1]);
  not not_3 (O_2_0[2], A_2_0[2]);

  // Other names for the same wires on the sheet: A0 = A_2_0[0]; A1 = A_2_0[1]; A2 = A_2_0[2]; O0 = O_2_0[0];
  //   O1 = O_2_0[1]; O2 = O_2_0[2]
endmodule
