// Digital circuit 3BitROL.dig as structural Verilog
module _3BitROL (
  input  [1:0] Shift_1_0,
  input  [2:0] A_2_0,
  output [2:0] O_2_0
);

  Multiplexer #(.Selector_Bits(2)) multiplexer_1 (
    .sel(Shift_1_0), .in_0(A_2_0[2]), .in_1(A_2_0[1]), .in_2(A_2_0[0]), .in_3(A_2_0[2]), .out(O_2_0[2]));
  Multiplexer #(.Selector_Bits(2)) multiplexer_2 (
    .sel(Shift_1_0), .in_0(A_2_0[1]), .in_1(A_2_0[0]), .in_2(A_2_0[2]), .in_3(A_2_0[1]), .out(O_2_0[1]));
  Multiplexer #(.Selector_Bits(2)) multiplexer_3 (
    .sel(Shift_1_0), .in_0(A_2_0[0]), .in_1(A_2_0[2]), .in_2(A_2_0[1]), .in_3(A_2_0[0]), .out(O_2_0[0]));

  // Other names for the same wires on the sheet: A0 = A_2_0[0]; A1 = A_2_0[1]; A2 = A_2_0[2]; O0 = O_2_0[0];
  //   O1 = O_2_0[1]; O2 = O_2_0[2]
endmodule
