// Digital circuit 3BitReg.dig as structural Verilog
module _3BitReg (
  input  [2:0] Din_2_0,
  input  Sel,
  input  Clock,
  output [2:0] Dout_2_0
);

  _1BitReg _1bitreg_1 (.Dout(Dout_2_0[0]), .Din(Din_2_0[0]), .Sel(Sel), .Clock(Clock));
  _1BitReg _1bitreg_2 (.Dout(Dout_2_0[1]), .Din(Din_2_0[1]), .Sel(Sel), .Clock(Clock));
  _1BitReg _1bitreg_3 (.Dout(Dout_2_0[2]), .Din(Din_2_0[2]), .Sel(Sel), .Clock(Clock));
endmodule
