// Digital circuit 3BitRegSet.dig as structural Verilog
module _3BitRegSet (
  input  [2:0] Wr_2_0,
  input  REG_EN,
  input  [2:0] Wrd_2_0,
  input  Clock,
  input  [2:0] Ra_2_0,
  input  [2:0] Rb_2_0,
  output [2:0] A_2_0,
  output [2:0] B_2_0
);

  wire Reg0, Reg1, Reg2, Reg3, Reg4, Reg5;
  wire [2:0] R0, R1, R2, R3, R4, R5;

  Demultiplexer #(.Selector_Bits(3)) demultiplexer_1 (
    .sel(Wr_2_0), .in(REG_EN), .out_0(Reg0), .out_1(Reg1), .out_2(Reg2), .out_3(Reg3), .out_4(Reg4),
    .out_5(Reg5));  // open: out_6, out_7
  _3BitReg _3bitreg_1 (.Din_2_0(Wrd_2_0), .Sel(Reg0), .Clock(Clock), .Dout_2_0(R0));
  _3BitReg _3bitreg_2 (.Din_2_0(Wrd_2_0), .Sel(Reg1), .Clock(Clock), .Dout_2_0(R1));
  _3BitReg _3bitreg_3 (.Din_2_0(Wrd_2_0), .Sel(Reg2), .Clock(Clock), .Dout_2_0(R2));
  _3BitReg _3bitreg_4 (.Din_2_0(Wrd_2_0), .Sel(Reg3), .Clock(Clock), .Dout_2_0(R3));
  _3BitReg _3bitreg_5 (.Din_2_0(Wrd_2_0), .Sel(Reg4), .Clock(Clock), .Dout_2_0(R4));
  _3BitReg _3bitreg_6 (.Din_2_0(Wrd_2_0), .Sel(Reg5), .Clock(Clock), .Dout_2_0(R5));
  Multiplexer #(.Selector_Bits(3), .Bits(3)) multiplexer_1 (
    .sel(Ra_2_0), .in_0(R0), .in_1(R1), .in_2(R2), .in_3(R3), .in_4(R4), .in_5(R5), .in_6(3'b000),
    .in_7(3'b000), .out(A_2_0));
  Multiplexer #(.Selector_Bits(3), .Bits(3)) multiplexer_2 (
    .sel(Rb_2_0), .in_0(R0), .in_1(R1), .in_2(R2), .in_3(R3), .in_4(R4), .in_5(R5), .in_6(3'b000),
    .in_7(3'b000), .out(B_2_0));
endmodule
