// Digital circuit 3bitProgramCounter.dig as structural Verilog
module _3bitProgramCounter (
  input  [2:0] I_2_0,
  input  CPU_CLK,
  output [2:0] O_2_0
);

  _3BitReg _3bitreg_1 (.Din_2_0(I_2_0), .Sel(1'b1), .Clock(CPU_CLK), .Dout_2_0(O_2_0));
endmodule
