// Digital circuit Control Unit.dig as structural Verilog
module Control_Unit (
  input  [3:0] Opcode_3_0,
  input  ZF,
  input  SF,
  output [1:0] Op_1_0,
  output REG_EN,
  output Imm_sel,
  output Jmp_sel
);

  wire and_2_out, and_3_out, and_4_out, and_5_out, not_1_out, or_1_out;

  and and_1 (Imm_sel, Opcode_3_0[2], ~Opcode_3_0[3]);  // And
  and and_2 (and_2_out, ~Opcode_3_0[2], Opcode_3_0[3]);  // And
  and and_3 (and_3_out, ~Opcode_3_0[2], ~Opcode_3_0[3]);  // And
  not not_1 (not_1_out, and_2_out);
  or or_1 (or_1_out, and_3_out, Imm_sel);
  and and_4 (and_4_out, ~Opcode_3_0[0], ~Opcode_3_0[1], and_2_out);  // And
  and and_5 (and_5_out, Opcode_3_0[0], ~Opcode_3_0[1], and_2_out, ZF, ~SF);  // And
  and and_6 (REG_EN, or_1_out, not_1_out);
  or or_2 (Jmp_sel, and_4_out, and_5_out);

  assign Op_1_0 = Opcode_3_0[1:0];
endmodule
